# Fritzing sketch touch-lamp (saved by Fritzing 0.9.3b)
circuit board: 8.46667cm x 5.64444cm
breadboards: 1

parts:
  U1 = atmega328 [package=dip]
  CONN1 = USB connector [package=THT]
  22pF = Capacitor [package=cap-pth-small2]
  22pF_2 = Capacitor [package=cap-pth-small2]
  XTAL1 = Crystal [frequency="16 Mhz" package=SMD]
  U2 = CAPSENSE_PAD [package=capsense_pad]
  R1 = Resistor [tolerance=±5% resistance=1M package="0402 [SMD]"]
  K1 = Relay [part_number=FRS1B-S package=THT]  # not connected

nets (from the breadboard view):
  VCC: U1.VCC, CONN1.5V
  N1: U1.GND#7, CONN1.GND, CONN1.chassis6, 22pF.1, 22pF_2.2
  N2: U1.XLAT1, 22pF_2.1, XTAL1.pin_1
  N3: U1.D7, R1.Pin_0
  N4: U1.D8, U2.RECEIVE, U2.RES, R1.Pin_1
  N5: 22pF.2, XTAL1.pin_0
